// Digital circuit ALU.dig as structural Verilog
module ALU (
  input  [31:0] A,
  input  [31:0] B,
  input  [3:0] ALUOp,
  output [31:0] R,
  output [3:0] NZCV,
  output N,
  output Z,
  output C,
  output V
);

  wire and_2_out, and_3_out;
  wire [30:0] Sub;
  wire [31:0] Add, And, LSL, LSR, Mul, Or, Xor;
  wire [63:32] mul_1_mul;

  Add #(.Bits(32)) add_1 (.a(A), .b(B), .c_i(1'b0), .s(Add));  // open: c_o
  Sub #(.Bits(32)) sub_1 (.a(A), .b(B), .c_i(1'b0), .s({N, Sub}));  // open: c_o
  Mul #(.Bits(32)) mul_1 (.a(A), .b(B), .mul({mul_1_mul, Mul}));
  BarrelShifter #(.Bits(32)) barrelshifter_1 (.in(A), .shift(B[5:0]), .out(LSL));
  BarrelShifter #(.Bits(32), .direction("right")) barrelshifter_2 (.in(A), .shift(B[5:0]), .out(LSR));
  assign And = A & B;  // And and_1, 32 bits wide
  assign Or = A | B;  // Or or_1, 32 bits wide
  assign Xor = A ^ B;  // XOr xor_1, 32 bits wide
  Multiplexer #(.Selector_Bits(4), .Bits(32)) multiplexer_1 (
    .sel(ALUOp), .in_0(Add), .in_1({N, Sub}), .in_2(Mul), .in_3(B), .in_4(LSL), .in_5(LSR), .in_6(And),
    .in_7(Or), .in_8(Xor), .in_9({32{1'b0}}), .in_10({32{1'b0}}), .in_11({32{1'b0}}), .in_12({32{1'b0}}),
    .in_13({32{1'b0}}), .in_14({32{1'b0}}), .in_15({32{1'b0}}), .out(R));
  and and_2 (and_2_out, ~A[31], B[31], N);  // And
  and and_3 (and_3_out, A[31], ~B[31], ~N);  // And
  Comparator #(.Bits(32)) comparator_1 (.a({N, Sub}), .b({32{1'b0}}), .eq(NZCV[1]));  // open: gt, lt
  Comparator #(.Bits(32)) comparator_2 (.a(A), .b(B), .lt(C));  // open: gt, eq
  or or_2 (NZCV[3], and_2_out, and_3_out);

  assign {NZCV[2], NZCV[0]} = {C, N};
  assign V = NZCV[3];
  assign Z = NZCV[1];

  // Other names for the same wires on the sheet: Sub[31] = N
endmodule
