// Digital circuit decoder.dig as structural Verilog
module decoder (
  input  [3:0] sel,
  input  en,
  output R0,
  output R1,
  output R2,
  output R3,
  output R4,
  output R5,
  output R6,
  output R7,
  output R8,
  output R9,
  output R10,
  output R11,
  output R12,
  output R13,
  output R14
);

  wire decoder_1_out_0, decoder_1_out_1, decoder_1_out_2, decoder_1_out_3, decoder_1_out_4, decoder_1_out_5,
       decoder_1_out_6, decoder_1_out_7, decoder_1_out_8, decoder_1_out_9, decoder_1_out_10,
       decoder_1_out_11, decoder_1_out_12, decoder_1_out_13, decoder_1_out_14;

  Decoder #(.Selector_Bits(4)) decoder_1 (
    .sel(sel), .out_0(decoder_1_out_0), .out_1(decoder_1_out_1), .out_2(decoder_1_out_2),
    .out_3(decoder_1_out_3), .out_4(decoder_1_out_4), .out_5(decoder_1_out_5), .out_6(decoder_1_out_6),
    .out_7(decoder_1_out_7), .out_8(decoder_1_out_8), .out_9(decoder_1_out_9), .out_10(decoder_1_out_10),
    .out_11(decoder_1_out_11), .out_12(decoder_1_out_12), .out_13(decoder_1_out_13), .out_14(decoder_1_out_14));  // open: out_15
  and and_1 (R0, en, decoder_1_out_0);
  and and_2 (R1, en, decoder_1_out_1);
  and and_3 (R2, en, decoder_1_out_2);
  and and_4 (R3, en, decoder_1_out_3);
  and and_5 (R4, en, decoder_1_out_4);
  and and_6 (R5, en, decoder_1_out_5);
  and and_7 (R6, en, decoder_1_out_6);
  and and_8 (R7, en, decoder_1_out_7);
  and and_9 (R8, en, decoder_1_out_8);
  and and_10 (R9, en, decoder_1_out_9);
  and and_11 (R10, en, decoder_1_out_10);
  and and_12 (R11, en, decoder_1_out_11);
  and and_13 (R12, en, decoder_1_out_12);
  and and_14 (R13, en, decoder_1_out_13);
  and and_15 (R14, en, decoder_1_out_14);
endmodule
