// Digital circuit decoder2.dig as structural Verilog
module decoder2 (
  input  [31:0] IW,
  output WDsel,
  output [1:0] WRsel,
  output [1:0] RR1sel,
  output [1:0] RR0sel,
  output [1:0] PCsel,
  output [3:0] ALUop,
  output ALUsrcB,
  output [2:0] EXTop,
  output RFW,
  output MW,
  output MR,
  output CPSRW,
  output SWP,
  output [31:0] new_iw
);

  wire ADD_I, ADD_R, AND, B, BL, BX, CMP_I, CMP_R, comparator_1_eq, comparator_2_gt, comparator_2_lt,
       comparator_3_eq, LDR_I, LDR_R, LSL_I, lsl_i__part_2_eq, lsl_i_eq, LSR_I, lsr_i__part_2_eq, lsr_i_eq,
       MOV_I, MOV_R, mov_r_eq, MUL, mul_eq, mul_part2_eq, MVN, OR, or_1_out, STR_I, SUB_I, SUB_R, SWP_1,
       SWP_eq, SWP_P2_eq, XOR;
  wire [4:0] priorityencoder_1_num;

  Comparator #(.Bits(4)) comparator_1 (.a(IW[15:12]), .b(IW[3:0]), .eq(comparator_1_eq));  // open: gt, lt
  Comparator #(.Bits(4)) comparator_2 (
    .a(IW[15:12]), .b(IW[3:0]), .gt(comparator_2_gt), .lt(comparator_2_lt));  // open: eq
  Comparator #(.Bits(4)) comparator_3 (.a(IW[15:12]), .b(IW[3:0]), .eq(comparator_3_eq));  // open: gt, lt
  Comparator #(.Bits(8)) u_mov_r (.a(IW[27:20]), .b(8'h1a), .eq(mov_r_eq));  // open: gt, lt
  or or_1 (or_1_out, comparator_2_gt, comparator_2_lt);
  // Probe on IW[27:20]
  // Probe on IW[27:24]
  // Probe on IW[27:4]
  // Probe on IW[7:4]
  // Probe on IW[6:4]
  // Probe on IW[3:0]
  // Probe on IW[15:12]
  // Probe on IW[11:4]
  Comparator #(.Bits(8)) u_add_r (.a(IW[27:20]), .b(8'h8), .eq(ADD_R));  // open: gt, lt
  Comparator #(.Bits(8)) u_add_i (.a(IW[27:20]), .b(8'h28), .eq(ADD_I));  // open: gt, lt
  Comparator #(.Bits(8)) u_mov_i (.a(IW[27:20]), .b(8'h3a), .eq(MOV_I));  // open: gt, lt
  Comparator #(.Bits(8)) u_sub_r (.a(IW[27:20]), .b(8'h4), .eq(SUB_R));  // open: gt, lt
  Comparator #(.Bits(8)) u_sub_i (.a(IW[27:20]), .b(8'h24), .eq(SUB_I));  // open: gt, lt
  Comparator #(.Bits(8)) u_mul (.a(IW[27:20]), .b({8{1'b0}}), .eq(mul_eq));  // open: gt, lt
  Comparator #(.Bits(4)) mul_part2 (.a(IW[7:4]), .b(4'b1001), .eq(mul_part2_eq));  // open: gt, lt
  Comparator #(.Bits(8)) u_lsl_i (.a(IW[27:20]), .b(8'h1a), .eq(lsl_i_eq));  // open: gt, lt
  Comparator #(.Bits(3)) lsl_i__part_2 (.a(IW[6:4]), .b(3'b000), .eq(lsl_i__part_2_eq));  // open: gt, lt
  Comparator #(.Bits(8)) u_lsr_i (.a(IW[27:20]), .b(8'h1a), .eq(lsr_i_eq));  // open: gt, lt
  Comparator #(.Bits(3)) lsr_i__part_2 (.a(IW[6:4]), .b(3'b010), .eq(lsr_i__part_2_eq));  // open: gt, lt
  Comparator #(.Bits(8)) u_ldr_r (.a(IW[27:20]), .b(8'h79), .eq(LDR_R));  // open: gt, lt
  Comparator #(.Bits(8)) u_ldr_i (.a(IW[27:20]), .b(8'h59), .eq(LDR_I));  // open: gt, lt
  Comparator #(.Bits(8)) u_str_i (.a(IW[27:20]), .b(8'h58), .eq(STR_I));  // open: gt, lt
  Comparator #(.Bits(8)) u_cmp_i (.a(IW[27:20]), .b(8'h35), .eq(CMP_I));  // open: gt, lt
  Comparator #(.Bits(8)) u_cmp_r (.a(IW[27:20]), .b(8'h15), .eq(CMP_R));  // open: gt, lt
  Comparator #(.Bits(4)) u_b (.a(IW[27:24]), .b(4'b1010), .eq(B));  // open: gt, lt
  Comparator #(.Bits(4)) u_bl (.a(IW[27:24]), .b(4'b1011), .eq(BL));  // open: gt, lt
  Comparator #(.Bits(24)) u_bx (.a(IW[27:4]), .b(24'h12fff1), .eq(BX));  // open: gt, lt
  Comparator #(.Bits(8)) u_mvn (.a(IW[27:20]), .b(8'h3e), .eq(MVN));  // open: gt, lt
  Comparator #(.Bits(8)) u_and (.a(IW[27:20]), .b({8{1'b0}}), .eq(AND));  // open: gt, lt
  Comparator #(.Bits(8)) or_2 (.a(IW[27:20]), .b(8'h18), .eq(OR));  // open: gt, lt
  Comparator #(.Bits(8)) u_xor (.a(IW[27:20]), .b(8'h3), .eq(XOR));  // open: gt, lt
  Comparator #(.Bits(8)) u_SWP (.a(IW[27:20]), .b(8'h10), .eq(SWP_eq));  // open: gt, lt
  Comparator #(.Bits(8)) SWP_P2 (.a(IW[11:4]), .b(8'h9), .eq(SWP_P2_eq));  // open: gt, lt
  and and_2 (MOV_R, mov_r_eq, or_1_out);
  and and_3 (MUL, mul_eq, mul_part2_eq);
  and and_4 (LSL_I, lsl_i_eq, comparator_3_eq, lsl_i__part_2_eq);
  and and_5 (LSR_I, lsr_i_eq, comparator_1_eq, lsr_i__part_2_eq);
  and and_6 (SWP_1, SWP_eq, SWP_P2_eq);
  PriorityEncoder #(.Selector_Bits(5)) priorityencoder_1 (
    .in0(ADD_R), .in1(ADD_I), .in2(LSL_I), .in3(MOV_I), .in4(SUB_R), .in5(SUB_I), .in6(MOV_R), .in7(LSR_I),
    .in8(AND), .in9(LDR_R), .in10(LDR_I), .in11(B), .in12(BL), .in13(BX), .in14(STR_I), .in15(CMP_I),
    .in16(CMP_R), .in17(MVN), .in18(MUL), .in19(OR), .in20(XOR), .in21(SWP_1), .in22(1'b0), .in23(1'b0),
    .in24(1'b0), .in25(1'b0), .in26(1'b0), .in27(1'b0), .in28(1'b0), .in29(1'b0), .in30(1'b0), .in31(1'b0),
    .num(priorityencoder_1_num));  // open: any
  Multiplexer #(.Selector_Bits(5), .Bits(20)) multiplexer_1 (
    .sel(priorityencoder_1_num), .in_0(20'h80000), .in_1(20'h88000), .in_2(20'hba180), .in_3(20'h89800),
    .in_4(20'h80800), .in_5(20'h88800), .in_6(20'h81800), .in_7(20'hba980), .in_8(20'h83000),
    .in_9(20'h80002), .in_10(20'h98002), .in_11(20'h28280), .in_12(20'ha828c), .in_13(20'h400),
    .in_14(20'h18021), .in_15(20'h8800), .in_16(20'h800), .in_17(20'hc9800), .in_18(20'h81110),
    .in_19(20'h83800), .in_20(20'h84000), .in_21(20'h98002), .in_22({20{1'b0}}), .in_23({20{1'b0}}),
    .in_24({20{1'b0}}), .in_25({20{1'b0}}), .in_26({20{1'b0}}), .in_27({20{1'b0}}), .in_28({20{1'b0}}),
    .in_29({20{1'b0}}), .in_30({20{1'b0}}), .in_31({20{1'b0}}),
    .out({RFW, EXTop, ALUsrcB, ALUop, PCsel, RR0sel, RR1sel, WRsel, WDsel, MR, MW}));
  and and_7 (SWP, SWP_1, 1'b1);
  // Probe on {RFW, EXTop, ALUsrcB, ALUop, PCsel, RR0sel, RR1sel, WRsel, WDsel, MR, MW}
  or or_3 (CPSRW, CMP_I, CMP_R);

  assign new_iw = {IW[31:28], 8'h58, IW[19:16], IW[3:0], {8{1'b0}}, IW[15:12]};

  // Other names for the same wires on the sheet: bits_0_3[3:0] = IW[3:0]; bits_4___11[7:0] = IW[11:4];
  //   bits_6_4[2:0] = IW[6:4]; bits_7_4[3:0] = IW[7:4]; bits_27_4[23:0] = IW[27:4]; bits_12_15[3:0] = IW[15:12];
  //   bits_27_20[7:0] = IW[27:20]; bits_27_24[3:0] = IW[27:24]
endmodule
