// Digital circuit decoder_main.dig as structural Verilog
module decoder_main (
  input  [31:0] IW,
  input  [3:0] NZCV,
  input  CLK,
  output WDsel,
  output [1:0] WRsel,
  output [1:0] RR1sel,
  output [1:0] RR0sel,
  output [1:0] PCsel,
  output [3:0] ALUop,
  output ALUsrcB,
  output [2:0] EXTop,
  output RFW,
  output MW,
  output MR,
  output swp,
  output [31:0] new_iw
);

  wire AL_eq, and_1_out, and_2_out, and_3_out, and_4_out, and_5_out, and_6_out, and_7_out, C, condex,
       decoder2_1_cpsrw, EQ_eq, GE_eq, GE_pt2_eq, GT_eq, GT_p2_eq, LE_eq, LE_p2_gt, LE_p2_lt, LT_eq,
       LT_p2_gt, LT_p2_lt, N, NE_eq, or_1_out, or_2_out, or_3_out, V, Z;
  wire [1:0] PCsel_t;

  Comparator LE_p2 (.a(N), .b(V), .gt(LE_p2_gt), .lt(LE_p2_lt));  // open: eq
  decoder2 decoder2_1 (
    .IW(IW), .new_iw(new_iw), .RFW(RFW), .EXTop(EXTop), .ALUsrcB(ALUsrcB), .ALUop(ALUop), .PCsel(PCsel_t),
    .RR0sel(RR0sel), .RR1sel(RR1sel), .WRsel(WRsel), .WDsel(WDsel), .MR(MR), .MW(MW),
    .CPSRW(decoder2_1_cpsrw), .SWP(swp));
  Register #(.Bits(4)) CPSR (.D(NZCV), .C(CLK), .en(decoder2_1_cpsrw), .Q({V, C, Z, N}));
  Comparator #(.Bits(4)) AL (.a(IW[31:28]), .b(4'b1110), .eq(AL_eq));  // open: gt, lt
  Comparator #(.Bits(4)) EQ (.a(IW[31:28]), .b(4'b0000), .eq(EQ_eq));  // open: gt, lt
  Comparator #(.Bits(4)) NE (.a(IW[31:28]), .b(4'b0001), .eq(NE_eq));  // open: gt, lt
  Comparator #(.Bits(4)) LT (.a(IW[31:28]), .b(4'b1011), .eq(LT_eq));  // open: gt, lt
  Comparator LT_p2 (.a(N), .b(V), .gt(LT_p2_gt), .lt(LT_p2_lt));  // open: eq
  Comparator #(.Bits(4)) GT (.a(IW[31:28]), .b(4'b1100), .eq(GT_eq));  // open: gt, lt
  Comparator GT_p2 (.a(N), .b(V), .eq(GT_p2_eq));  // open: gt, lt
  Comparator #(.Bits(4)) LE (.a(IW[31:28]), .b(4'b1101), .eq(LE_eq));  // open: gt, lt
  Comparator #(.Bits(4)) GE (.a(IW[31:28]), .b(4'b1010), .eq(GE_eq));  // open: gt, lt
  Comparator GE_pt2 (.a(N), .b(V), .eq(GE_pt2_eq));  // open: gt, lt
  or or_1 (or_1_out, LE_p2_gt, LE_p2_lt);
  or or_2 (or_2_out, LT_p2_gt, LT_p2_lt);
  and and_1 (and_1_out, Z, LE_eq);
  and and_2 (and_2_out, LE_eq, or_1_out);
  and and_3 (and_3_out, GE_eq, GE_pt2_eq);
  // Probe on N
  // Probe on Z
  // Probe on C
  // Probe on V
  and and_4 (and_4_out, Z, EQ_eq);
  and and_5 (and_5_out, ~Z, NE_eq);  // And
  and and_6 (and_6_out, LT_eq, or_2_out);
  and and_7 (and_7_out, ~Z, GT_eq, GT_p2_eq);  // And
  or or_3 (or_3_out, and_1_out, and_2_out);
  or or_4 (condex, AL_eq, and_4_out, and_5_out, and_6_out, and_7_out, or_3_out, and_3_out);
  Multiplexer #(.Bits(2)) multiplexer_1 (.sel(condex), .in_0(2'b00), .in_1(PCsel_t), .out(PCsel));
endmodule
