// Digital circuit extension_unit.dig as structural Verilog
module extension_unit (
  input  [31:0] IW,
  input  [2:0] EXT,
  output [31:0] extimm
);

  wire [7:0] add_1_s, neg_1_out;
  wire [31:0] barrelshifter_1_out, bitextender_1_out, bitextender_2_out;

  BitExtender #(.inputBits(24), .outputBits(32)) bitextender_1 (.in(IW[23:0]), .out(bitextender_1_out));
  Add #(.Bits(8)) add_1 (.a(IW[7:0]), .b(8'h1), .c_i(1'b0), .s(add_1_s));  // open: c_o
  BarrelShifter #(.Bits(32), .barrelSigned("true")) barrelshifter_1 (
    .in(bitextender_1_out), .shift(7'b0000010), .out(barrelshifter_1_out));
  Neg #(.Bits(8)) neg_1 (.in(add_1_s), .out(neg_1_out));
  BitExtender #(.outputBits(32)) bitextender_2 (.in(neg_1_out), .out(bitextender_2_out));
  Multiplexer #(.Selector_Bits(3), .Bits(32)) multiplexer_1 (
    .sel(EXT), .in_0({{24{1'b0}}, IW[7:0]}), .in_1({{20{1'b0}}, IW[11:0]}), .in_2(barrelshifter_1_out),
    .in_3({{27{1'b0}}, IW[11:7]}), .in_4(bitextender_2_out), .in_5({32{1'b0}}), .in_6({32{1'b0}}),
    .in_7({32{1'b0}}), .out(extimm));
endmodule
