// Digital circuit instruction_memory.dig as structural Verilog
module instruction_memory (
  input  [6:0] A,
  input  [3:0] PN,
  output [31:0] D
);

  wire [31:0] and_s_extra_credit_d, fact_s_d, or_s_extra_credit_d, quadratic_s_d, search_s_d,
       search_s_extra_credit_d, sort_s_d, sum_array_s_d, test_d, xor_s_extra_credit_d;

  ROM #(.AddrBits(7), .Bits(32)) quadratic_s (.A(A), .sel(1'b1), .D(quadratic_s_d));
  ROM #(.AddrBits(7), .Bits(32)) fact_s (.A(A), .sel(1'b1), .D(fact_s_d));
  ROM #(.AddrBits(7), .Bits(32)) sum_array_s (.A(A), .sel(1'b1), .D(sum_array_s_d));
  ROM #(.AddrBits(7), .Bits(32)) search_s (.A(A), .sel(1'b1), .D(search_s_d));
  ROM #(.AddrBits(7), .Bits(32)) sort_s (.A(A), .sel(1'b1), .D(sort_s_d));
  ROM #(.AddrBits(7), .Bits(32)) search_s_extra_credit (.A(A), .sel(1'b1), .D(search_s_extra_credit_d));
  ROM #(.AddrBits(7), .Bits(32)) and_s_extra_credit (.A(A), .sel(1'b1), .D(and_s_extra_credit_d));
  ROM #(.AddrBits(7), .Bits(32)) or_s_extra_credit (.A(A), .sel(1'b1), .D(or_s_extra_credit_d));
  ROM #(.AddrBits(7), .Bits(32)) xor_s_extra_credit (.A(A), .sel(1'b1), .D(xor_s_extra_credit_d));
  ROM #(.AddrBits(7), .Bits(32)) test (.A(A), .sel(1'b1), .D(test_d));
  Multiplexer #(.Selector_Bits(4), .Bits(32)) multiplexer_1 (
    .sel(PN), .in_0(quadratic_s_d), .in_1(fact_s_d), .in_2(sum_array_s_d), .in_3(search_s_d),
    .in_4(sort_s_d), .in_5(search_s_extra_credit_d), .in_6(and_s_extra_credit_d), .in_7(or_s_extra_credit_d),
    .in_8(xor_s_extra_credit_d), .in_9(test_d), .in_10({32{1'b0}}), .in_11({32{1'b0}}), .in_12({32{1'b0}}),
    .in_13({32{1'b0}}), .in_14({32{1'b0}}), .in_15({32{1'b0}}), .out(D));

  // Notes on the sheet:
  //   contents of quadratic_s (hex, n*v repeats v):
  //   e3a00002,e3a01004,e3a02008,e3a03010,eb000000,e2800000,e00c0090,e00c0c91,e0010092,
  //   e08cc001,e08c0003,e12fff1e
  //   contents of fact_s (hex, n*v repeats v):
  //   e3a0d080,e3a00005,eb000000,e2800000,e24dd008,e58de000,e3500000,1a000001,e3a00001,
  //   ea000004,e58d0004,e2400001,ebfffff6,e59d1004,e0000091,e59de000,e28dd008,e12fff1e
  //   contents of sum_array_s (hex, n*v repeats v):
  //   e3a0d080,e08dd00d,e08dd00d,e24dd014,e3a00000,e58d0000,e3a00004,e58d0004,e3a00008,
  //   e58d0008,e3a0000c,e58d000c,e3a00010,e58d0010,e1a0000d,e3a01005,eb000000,e2800000,
  //   e3a02000,e3a03000,e1530001,aa000004,e590c000,e082200c,e2800004,e2833001,eafffff8,
  //   e1a00002,e12fff1e
  //   contents of search_s (hex, n*v repeats v):
  //   e3a0d080,e08dd00d,e08dd00d,e24dd014,e3a00000,e58d0000,e3a00004,e58d0004,e3a00008,
  //   e58d0008,e3a0000c,e58d000c,e3a00010,e58d0010,e1a0000d,e3a01000,e3a02005,e3a0300c,
  //   eb000000,e2800000,e24dd008,e58de000,e58d4004,ebffffff,e042c001,e1a0c0ac,e08cc001,
  //   e1a0c10c,e790400c,e1a0c12c,e1530004,ca000006,ba000001,e1a0000c,ea000007,e1a0200c,
  //   e2422001,ebffffed,ea000003,e1a0100c,e2811001,ebffffe9,eaffffff,e59d4004,e59de000,
  //   e28dd008,e12fff1e
  //   contents of sort_s (hex, n*v repeats v):
  //   e3a0d080,e08dd00d,e08dd00d,e24dd018,e3a00010,e58d0000,e3a00004,e58d0004,e3a00020,
  //   e58d0008,e3a00002,e58d000c,e3a00008,e58d0010,e1a0000d,e3a01005,eb000014,e2800000,
  //   e24dd008,e58d4000,e3a02001,e3a04000,e5903000,e1510002,da000008,e1a02102,e790c002,
  //   e1a02122,e153000c,aa000001,e1a0300c,e1a04002,e2822001,eafffff4,e1a00004,e59d4000,
  //   e28dd008,e12fff1e,e24dd018,e58de000,e58d4010,e58d5014,e3a02000,e1510002,da000020,
  //   e58d0004,e58d1008,e58d200c,e0411002,e1a02102,e0800002,e1a02122,ebffffdc,e1a03000,
  //   e59d0004,e59d1008,e59d200c,e0823003,e1520003,a00000f,e1a02102,e790c002,e1a02122,e1a03103,
  //   e7904003,e1a03123,e1a02102,e0825000,e5854000,e1a02122,e1a03103,e0835000,e585c000,
  //   e1a03123,e2822001,eaffffde,e2822001,eaffffdc,e1a00001,e59d5014,e59d4010,e59de000,
  //   e28dd018,e12fff1e
  //   contents of search_s_extra_credit (hex, n*v repeats v):
  //   e3a0d080,e08dd00d,e08dd00d,e24dd014,e3a00000,e58d0000,e3a00004,e58d0004,e3a00008,
  //   e58d0008,e3a0000c,e58d000c,e3a00010,e58d0010,e1a0000d,e3a01000,e3a02005,e3a0300d,
  //   eb000000,e2800000,e24dd008,e58de014,e58d4018,e1510002,da000001,e3e00000,ea000013,
  //   e042c001,e1a0c0ac,e08cc001,e1a0c10c,e790400c,e1a0c12c,e1530004,ca000007,ba000001,
  //   e1a0000c,ea000008,e1a0200c,e2422001,e12fff1e,ebffffe9,ea000003,e1a0100c,e2811001,
  //   ebffffe5,eaffffff,e59d4018,e59de014,e28dd008,e12fff1e
  //   contents of and_s_extra_credit (hex, n*v repeats v):
  //   e3a00001,e3a01000,e0000001,e2800000
  //   contents of or_s_extra_credit (hex, n*v repeats v):
  //   e3a00001,e3a01000,e1800001,e2800000
  //   contents of xor_s_extra_credit (hex, n*v repeats v):
  //   e3a00001,e3a01001,e0300001,e2800000
  //   contents of test (hex, n*v repeats v):
  //   e3a00001,e3a01002,e3a02000,e1020091,e2800000
endmodule
