// Digital circuit processor_main.dig as structural Verilog
module processor_main (
  input  clk,
  input  [3:0] PN
);

  wire a_mul, ALUSrcb, C, CLK_t, CLR, comparator_1_eq, done, i_dp, MR, MW, N, RFW, swap_value, V, WDsel, Z;
  wire [1:0] PCsel, RR0sel, RR1sel, WRsel;
  wire [2:0] EXTop;
  wire [3:0] ALUOp, bits_0_3, bits_8_11, bits_12_15, bits_16_19, cond, multiplexer_4_out, multiplexer_5_out,
       multiplexer_6_out, NZCV;
  wire [23:0] b_offset;
  wire [27:24] IW;
  wire [31:0] add_1_s, add_2_s, Add_or_Not, alu_1_r, extension_unit_1_extimm, multiplexer_2_out,
       multiplexer_7_out, multiplexer_8_out, multiplexer_9_out, new_iw, r0, r1, r2, r3, r4, r5, r6, r7, r8,
       r9, r10, r11, r12, r13, r14, r15, ramdualport_1_d, register_1_q, registerfile2_1_rd0,
       registerfile2_1_rd1;
  wire [31:4] multiplexer_3_out;

  Comparator comparator_1 (.a(swap_value), .b(1'b1), .eq(comparator_1_eq));  // open: gt, lt
  Multiplexer #(.Bits(32)) multiplexer_1 (.sel(comparator_1_eq), .in_0(32'h4), .in_1({32{1'b0}}), .out(Add_or_Not));
  DipSwitch #(.dipDefault("true")) dipswitch_1 (.out(CLR));
  and and_1 (CLK_t, clk, ~done);  // And
  // Probe on {cond, IW[27:26], i_dp, IW[24], b_offset[23:22], a_mul, b_offset[20:0]}
  register register_1 (.D(multiplexer_2_out), .CLK(CLK_t), .EN(1'b1), .CLR(CLR), .Q(register_1_q));
  Multiplexer #(.Selector_Bits(2), .Bits(32)) multiplexer_2 (
    .sel(PCsel), .in_0(add_1_s), .in_1(multiplexer_9_out), .in_2(registerfile2_1_rd1), .in_3({32{1'b0}}),
    .out(multiplexer_2_out));
  Add #(.Bits(32)) add_1 (.a(register_1_q), .b(32'h4), .c_i(1'b0), .s(add_1_s));  // open: c_o
  decoder_main decoder_main_1 (
    .IW({cond, IW[27:26], i_dp, IW[24], b_offset[23:22], a_mul, b_offset[20:0]}), .NZCV(NZCV), .CLK(CLK_t),
    .RFW(RFW), .EXTop(EXTop), .ALUsrcB(ALUSrcb), .ALUop(ALUOp), .PCsel(PCsel), .RR0sel(RR0sel),
    .RR1sel(RR1sel), .WRsel(WRsel), .WDsel(WDsel), .MR(MR), .MW(MW), .swp(swap_value), .new_iw(new_iw));
  instruction_memory instruction_memory_1 (
    .A(register_1_q[8:2]), .PN(PN),
    .D({cond, IW[27:26], i_dp, IW[24], b_offset[23:22], a_mul, b_offset[20:0]}));
  // Probe on r0
  // Probe on r1
  // Probe on r2
  // Probe on r3
  // Probe on cond
  // Probe on cond
  // Probe on cond
  // Probe on cond
  Multiplexer #(.Bits(32)) multiplexer_3 (
    .sel(swap_value), .in_0({cond, IW[27:26], i_dp, IW[24], b_offset[23:22], a_mul, b_offset[20:0]}),
    .in_1(new_iw),
    .out({multiplexer_3_out[31:20], bits_16_19, bits_12_15, bits_8_11, multiplexer_3_out[7:4], bits_0_3}));
  Add #(.Bits(32)) add_2 (.a(add_1_s), .b(32'h4), .c_i(1'b0), .s(add_2_s));  // open: c_o
  // Probe on IW[27:26]
  // Probe on {IW[27:26], i_dp}
  // Probe on r4
  // Probe on r5
  // Probe on r6
  // Probe on r7
  // Probe on i_dp
  // Probe on {IW[27:26], i_dp, IW[24], b_offset[23]}
  // Probe on IW[27:26]
  // Probe on a_mul
  // Probe on i_dp
  // Probe on IW[24]
  Multiplexer #(.Selector_Bits(2), .Bits(4)) multiplexer_4 (
    .sel(RR0sel), .in_0(bits_16_19), .in_1(4'b1111), .in_2(bits_8_11), .in_3(bits_0_3),
    .out(multiplexer_4_out));
  Multiplexer #(.Selector_Bits(2), .Bits(4)) multiplexer_5 (
    .sel(RR1sel), .in_0(bits_0_3), .in_1(bits_12_15), .in_2(bits_16_19), .in_3(bits_8_11),
    .out(multiplexer_5_out));
  Multiplexer #(.Selector_Bits(2), .Bits(4)) multiplexer_6 (
    .sel(WRsel), .in_0(bits_12_15), .in_1(4'b1110), .in_2(bits_16_19), .in_3(bits_0_3),
    .out(multiplexer_6_out));
  Multiplexer #(.Bits(32)) multiplexer_7 (
    .sel(WDsel), .in_0(multiplexer_9_out), .in_1(add_1_s), .out(multiplexer_7_out));
  // Probe on r8
  // Probe on r9
  // Probe on r10
  // Probe on r11
  // Probe on {IW[24], b_offset[23:22], a_mul}
  // Probe on {b_offset[23:22], a_mul, b_offset[20:0]}
  // Probe on b_offset[20]
  // Probe on b_offset[20]
  // Probe on IW[24]
  // Probe on r12
  // Probe on r13
  // Probe on r14
  // Probe on r15
  // Probe on b_offset[19:16]
  // Probe on b_offset[19:16]
  // Probe on b_offset[23]
  registerfile2 registerfile2_1 (
    .ReadReg0(multiplexer_4_out), .ReadReg1(multiplexer_5_out), .writeReg(multiplexer_6_out),
    .writeData(multiplexer_7_out), .writeEn(RFW), .PC(add_2_s), .CLK(CLK_t), .CLR(CLR),
    .RD0(registerfile2_1_rd0), .RD1(registerfile2_1_rd1), .R0(r0), .R1(r1), .R2(r2), .R3(r3), .R4(r4),
    .R5(r5), .R6(r6), .R7(r7), .R8(r8), .R9(r9), .R10(r10), .R11(r11), .R12(r12), .R13(r13), .R14(r14),
    .R15(r15));
  // Probe on b_offset[15:12]
  // Probe on N
  // Probe on Z
  // Probe on C
  // Probe on V
  // Probe on b_offset[3:0]
  // Probe on b_offset[7:0]
  // Probe on b_offset[15:12]
  // Probe on b_offset[22]
  // Probe on a_mul
  // Probe on registerfile2_1_rd0
  // Probe on b_offset[11:8]
  // Probe on b_offset[7:4]
  // Probe on b_offset[20]
  Multiplexer #(.Bits(32)) multiplexer_8 (
    .sel(ALUSrcb), .in_0(registerfile2_1_rd1), .in_1(extension_unit_1_extimm), .out(multiplexer_8_out));
  extension_unit extension_unit_1 (
    .IW({cond, IW[27:26], i_dp, IW[24], b_offset[23:22], a_mul, b_offset[20:0]}), .EXT(EXTop),
    .extimm(extension_unit_1_extimm));
  Comparator #(.Bits(32)) comparator_2 (
    .a({cond, IW[27:26], i_dp, IW[24], b_offset[23:22], a_mul, b_offset[20:0]}), .b(32'he2800000), .eq(done));  // open: gt, lt
  // Probe on b_offset[11:0]
  // Probe on b_offset[3:0]
  ALU alu_1 (
    .A(registerfile2_1_rd0), .B(multiplexer_8_out), .ALUOp(ALUOp), .R(alu_1_r), .N(N), .Z(Z), .NZCV(NZCV),
    .C(C), .V(V));
  LED led_1 (.in(done));
  // Probe on b_offset[3:0]
  Multiplexer #(.Bits(32)) multiplexer_9 (.sel(MR), .in_0(alu_1_r), .in_1(ramdualport_1_d), .out(multiplexer_9_out));
  // Probe on extension_unit_1_extimm
  RAMDualPort #(.AddrBits(7), .Bits(32)) ramdualport_1 (
    .A(alu_1_r[8:2]), .Din(registerfile2_1_rd1), .str(MW), .C(CLK_t), .ld(MR), .D(ramdualport_1_d));

  // Other names for the same wires on the sheet: imm[7:0] = b_offset[7:0]; immoff[11:0] = b_offset[11:0];
  //   IW (some bits) = {cond, i_dp, b_offset[23:22], a_mul, b_offset[20:0]}; rm[3:0] = b_offset[3:0];
  //   rm_mul[3:0] = b_offset[3:0]; opmul4[3:0] = b_offset[7:4]; rs_mul[3:0] = b_offset[11:8];
  //   rd[3:0] = b_offset[15:12]; rn_mul[3:0] = b_offset[15:12]; rd_mul[3:0] = b_offset[19:16];
  //   rn[3:0] = b_offset[19:16]; l_sdt = b_offset[20]; s_dp = b_offset[20]; s_mul = b_offset[20];
  //   b_offset[21] = a_mul; opc[3:0] = {IW[24], b_offset[23:22], a_mul}; w_sdt = a_mul; b_sdt = b_offset[22];
  //   opmul6[4:0] = {IW[27:26], i_dp, IW[24], b_offset[23]}; u_sdt = b_offset[23]; l_b = IW[24]; p_sdt = IW[24];
  //   i_sdt = i_dp; opb3[2:0] = {IW[27:26], i_dp}; op2[1:0] = IW[27:26]; opmul2[1:0] = IW[27:26]

  // Notes on the sheet:
  //   clk: Hz: 100
  //   0 - quadratic_s - output: 48
  //   1 - fact_s - output: 120
  //   2 - sum array_s - output: 40
  //   3 - search_s - output: 3
  //   4 - sort_s - output: 5
  //   5 - search_s ec - output: -1 
  //   6 - and_s - output 0
  //   7 - or_s - output 1
  //   8 - xor_s - output 0
  //   DP
  //   MUL
  //   SDT
  //   B
endmodule
