// Digital circuit registerfile2.dig as structural Verilog
module registerfile2 (
  input  [3:0] ReadReg0,
  input  [3:0] ReadReg1,
  input  writeEn,
  input  [3:0] writeReg,
  input  [31:0] writeData,
  input  CLR,
  input  CLK,
  input  [31:0] PC,
  output [31:0] RD0,
  output [31:0] RD1,
  output [31:0] R0,
  output [31:0] R1,
  output [31:0] R2,
  output [31:0] R3,
  output [31:0] R4,
  output [31:0] R5,
  output [31:0] R6,
  output [31:0] R7,
  output [31:0] R8,
  output [31:0] R9,
  output [31:0] R10,
  output [31:0] R11,
  output [31:0] R12,
  output [31:0] R13,
  output [31:0] R14,
  output [31:0] R15
);

  wire R0_t, R1_t, R2_t, R3_t, R4_t, R5_t, R6_t, R7_t, R8_t, R9_t, R10_t, R11_t, R12_t, R13_t, R14_t;

  decoder decoder_1 (
    .sel(writeReg), .en(writeEn), .R0(R0_t), .R1(R1_t), .R2(R2_t), .R3(R3_t), .R4(R4_t), .R5(R5_t),
    .R6(R6_t), .R7(R7_t), .R8(R8_t), .R9(R9_t), .R10(R10_t), .R11(R11_t), .R12(R12_t), .R13(R13_t),
    .R14(R14_t));
  register register_1 (.D(writeData), .CLK(CLK), .EN(R0_t), .CLR(CLR), .Q(R0));
  register register_2 (.D(writeData), .CLK(CLK), .EN(R1_t), .CLR(CLR), .Q(R1));
  register register_3 (.D(writeData), .CLK(CLK), .EN(R2_t), .CLR(CLR), .Q(R2));
  register register_4 (.D(writeData), .CLK(CLK), .EN(R3_t), .CLR(CLR), .Q(R3));
  register register_5 (.D(writeData), .CLK(CLK), .EN(R4_t), .CLR(CLR), .Q(R4));
  register register_6 (.D(writeData), .CLK(CLK), .EN(R5_t), .CLR(CLR), .Q(R5));
  register register_7 (.D(writeData), .CLK(CLK), .EN(R6_t), .CLR(CLR), .Q(R6));
  register register_8 (.D(writeData), .CLK(CLK), .EN(R7_t), .CLR(CLR), .Q(R7));
  register register_9 (.D(writeData), .CLK(CLK), .EN(R8_t), .CLR(CLR), .Q(R8));
  register register_10 (.D(writeData), .CLK(CLK), .EN(R9_t), .CLR(CLR), .Q(R9));
  register register_11 (.D(writeData), .CLK(CLK), .EN(R10_t), .CLR(CLR), .Q(R10));
  register register_12 (.D(writeData), .CLK(CLK), .EN(R11_t), .CLR(CLR), .Q(R11));
  register register_13 (.D(writeData), .CLK(CLK), .EN(R12_t), .CLR(CLR), .Q(R12));
  register register_14 (.D(writeData), .CLK(CLK), .EN(R13_t), .CLR(CLR), .Q(R13));
  register register_15 (.D(writeData), .CLK(CLK), .EN(R14_t), .CLR(CLR), .Q(R14));
  Multiplexer #(.Selector_Bits(4), .Bits(32)) multiplexer_1 (
    .sel(ReadReg0), .in_0(R0), .in_1(R1), .in_2(R2), .in_3(R3), .in_4(R4), .in_5(R5), .in_6(R6), .in_7(R7),
    .in_8(R8), .in_9(R9), .in_10(R10), .in_11(R11), .in_12(R12), .in_13(R13), .in_14(R14), .in_15(PC),
    .out(RD0));
  Multiplexer #(.Selector_Bits(4), .Bits(32)) multiplexer_2 (
    .sel(ReadReg1), .in_0(R0), .in_1(R1), .in_2(R2), .in_3(R3), .in_4(R4), .in_5(R5), .in_6(R6), .in_7(R7),
    .in_8(R8), .in_9(R9), .in_10(R10), .in_11(R11), .in_12(R12), .in_13(R13), .in_14(R14), .in_15(PC),
    .out(RD1));

  assign R15 = PC;

  // Other names for the same wires on the sheet: Q0[31:0] = R0; Q1[31:0] = R1; Q2[31:0] = R2; Q3[31:0] = R3;
  //   Q4[31:0] = R4; Q5[31:0] = R5; Q6[31:0] = R6; Q7[31:0] = R7; Q8[31:0] = R8; Q9[31:0] = R9; Q10[31:0] = R10;
  //   Q11[31:0] = R11; Q12[31:0] = R12; Q13[31:0] = R13; Q14[31:0] = R14
endmodule
